# Fritzing sketch RpiPowerHandler (saved by Fritzing 0.9.3b)
breadboards: 1

parts:
  Reset_Button = Pushbutton [package="[THT]"]
  Power_Switch = Toggle Switch [package=THT]
  Raspberry_Pi_1 = Raspberry Pi 3 [part_number=RPI-3-V1.2]
  WeMos_D1_Mini1 = WeMos D1 Mini
  WeMos_D1_Mini_Relay_Shield_V1 = WeMos D1 Mini Relay Shield V2
  R1 = Resistor [tolerance=±5% resistance=10k package=THT]
  R3 = Resistor [tolerance=±5% resistance=10k package=THT]
  R4 = Resistor [tolerance=±5% resistance=10k package=THT]
  R5 = Resistor [tolerance=±5% resistance=10k package=THT]
  R6 = Resistor [tolerance=±5% resistance=10k package=THT]
  Power_LED = LED - 5mm [color="Green (570nm)" package="5 mm [THT]"]
  R7 = Resistor [tolerance=±5% resistance=120 package=THT]

nets:
  GND: Reset_Button.Pin_1, Reset_Button.Pin_2, Power_Switch.L2, Raspberry_Pi_1.GND, WeMos_D1_Mini1.G, WeMos_D1_Mini_Relay_Shield_V1.G
  N1: Reset_Button.Pin_3, Reset_Button.Pin_4, WeMos_D1_Mini1.D7, R6.Pin_1
  N2: Power_Switch.COM, WeMos_D1_Mini1.D2, R1.Pin_0
  N3: Raspberry_Pi_1.GPIO4, WeMos_D1_Mini1.D6, R5.Pin_0
  N4: Raspberry_Pi_1.GPIO17, WeMos_D1_Mini1.D0, R3.Pin_0
  N5: Raspberry_Pi_1.GPIO27, WeMos_D1_Mini1.D5, R4.Pin_0
  5V: Raspberry_Pi_1.5V
  3.3V: WeMos_D1_Mini1.3V3, WeMos_D1_Mini_Relay_Shield_V1.3V3, R1.Pin_1, R3.Pin_1, R4.Pin_1, R5.Pin_1, R6.Pin_0, R7.Pin_1
  N6: WeMos_D1_Mini1.D1, WeMos_D1_Mini_Relay_Shield_V1.D1
  N7: WeMos_D1_Mini1.D4, Power_LED.cathode
  N8: Power_LED.anode, R7.Pin_0
